// Logisim project cpu_hw4_group16.circ as structural Verilog: 5 circuits, main circuit CPU
module CPU (
);

  wire alu_1_blebne, and_1_out, and_2_out, clock_1_out, controllogic_1_alusrc, controllogic_1_branch,
       controllogic_1_call, controllogic_1_halt, controllogic_1_jump, controllogic_1_li, controllogic_1_m2r,
       controllogic_1_memread, controllogic_1_memwrite, controllogic_1_regdst, controllogic_1_regwrite,
       controllogic_1_rtn, not_1_out, not_2_out, not_3_out, not_4_out, or_1_out, or_2_out;
  wire [2:0] controllogic_1_aluop, multiplexer_3_out;
  wire [11:0] rom_1_data;
  wire [15:0] adder_1_out, adder_2_out, alu_1_aluresult, bit_extender_1_out, bit_extender_2_out,
       multiplexer_1_out, multiplexer_2_out, multiplexer_4_out, multiplexer_5_out, multiplexer_6_out,
       multiplexer_7_out, PC_q, ram_1_dout, register_1_q, registerfile_1_data1, registerfile_1_data2;
  wire [15:12] rom_1_data_2;

  Clock clock_1 (.out(clock_1_out));
  Register #(.width(16)) PC (.D(multiplexer_2_out), .en(not_1_out), .Q(PC_q), .clk(clock_1_out));  // open: clr
  not not_1 (not_1_out, controllogic_1_halt);
  // Probe on PC_q
  // Probe on multiplexer_4_out
  ROM #(.addrWidth(16), .dataWidth(16)) rom_1 (.addr(PC_q), .data({rom_1_data_2, rom_1_data}));
  Adder #(.width(16)) adder_1 (.a(16'h1), .b(PC_q), .out(adder_1_out));  // open: cin, cout
  Adder #(.width(16)) adder_2 (.a(PC_q), .b(multiplexer_4_out), .out(adder_2_out));  // open: cin, cout
  or or_1 (or_1_out, and_2_out, controllogic_1_jump, controllogic_1_call);
  or or_2 (or_2_out, controllogic_1_call, controllogic_1_jump);
  and and_1 (and_1_out, controllogic_1_call, not_2_out);
  not not_2 (not_2_out, controllogic_1_halt);
  Register #(.width(16)) register_1 (
    .D(adder_1_out), .en(and_1_out), .clk(clock_1_out), .Q(register_1_q));  // open: clr
  Multiplexer #(.width(16)) multiplexer_1 (
    .in0(adder_1_out), .in1(adder_2_out), .out(multiplexer_1_out), .sel(or_1_out));
  Multiplexer #(.width(16)) multiplexer_2 (
    .in0(multiplexer_1_out), .in1(register_1_q), .out(multiplexer_2_out), .sel(controllogic_1_rtn));
  // Probe on rom_1_data[5:0]
  // Probe on rom_1_data
  assign bit_extender_1_out = {{10{rom_1_data[5]}}, rom_1_data[5:0]};  // Bit_Extender bit_extender_1
  // Probe on rom_1_data[11:9]
  // Probe on rom_1_data[8:6]
  Multiplexer #(.width(3)) multiplexer_3 (
    .in0(rom_1_data[8:6]), .in1(rom_1_data[5:3]), .out(multiplexer_3_out), .sel(controllogic_1_regdst));
  // Probe on multiplexer_3_out
  assign bit_extender_2_out = {{4{rom_1_data[11]}}, rom_1_data};  // Bit_Extender bit_extender_2
  Multiplexer #(.width(16)) multiplexer_4 (
    .in0(bit_extender_1_out), .in1(bit_extender_2_out), .out(multiplexer_4_out), .sel(or_2_out));
  not not_3 (not_3_out, controllogic_1_halt);
  // Probe on multiplexer_7_out
  and and_2 (and_2_out, controllogic_1_branch, alu_1_blebne);
  ControlLogic controllogic_1 (
    .bits15to12(rom_1_data_2), .RegDst(controllogic_1_regdst), .Jump(controllogic_1_jump),
    .Branch(controllogic_1_branch), .MemRead(controllogic_1_memread), .M2R(controllogic_1_m2r),
    .ALUOp(controllogic_1_aluop), .MemWrite(controllogic_1_memwrite), .ALUSrc(controllogic_1_alusrc),
    .RegWrite(controllogic_1_regwrite), .Li(controllogic_1_li), .Call(controllogic_1_call),
    .Rtn(controllogic_1_rtn), .halt(controllogic_1_halt));
  RegisterFile registerfile_1 (
    .enable(not_3_out), .writeEnable(controllogic_1_regwrite), .readReg1(rom_1_data[11:9]),
    .readReg2(rom_1_data[8:6]), .writeReg(multiplexer_3_out), .writeData(multiplexer_7_out),
    .clock(clock_1_out), .Data1(registerfile_1_data1), .Data2(registerfile_1_data2));
  Multiplexer #(.width(16)) multiplexer_5 (
    .in0(registerfile_1_data1), .in1({16{1'b0}}), .out(multiplexer_5_out), .sel(controllogic_1_li));
  Multiplexer #(.width(16)) multiplexer_6 (
    .in0(registerfile_1_data2), .in1(multiplexer_4_out), .out(multiplexer_6_out), .sel(controllogic_1_alusrc));
  // Probe on multiplexer_6_out
  // Probe on controllogic_1_aluop
  // Probe on multiplexer_5_out
  // Probe on alu_1_aluresult
  // Probe on registerfile_1_data2
  ALU alu_1 (
    .operand1(multiplexer_5_out), .operation(controllogic_1_aluop), .operand2(multiplexer_6_out),
    .ALUResult(alu_1_aluresult), .BleBne(alu_1_blebne));
  RAM #(.addrWidth(16), .asyncread("true"), .dataWidth(16)) ram_1 (
    .addr(alu_1_aluresult), .we(controllogic_1_memwrite), .oe(controllogic_1_memread), .clk(not_4_out),
    .din(registerfile_1_data2), .dout(ram_1_dout));
  not not_4 (not_4_out, clock_1_out);
  // Probe on ram_1_dout
  // Probe on alu_1_aluresult
  Multiplexer #(.width(16)) multiplexer_7 (
    .in0(alu_1_aluresult), .in1(ram_1_dout), .out(multiplexer_7_out), .sel(controllogic_1_m2r));
  // Probe on multiplexer_7_out

  // Notes on the sheet:
  //   contents of rom_1 (hex, n*v repeats v):
  //   6 44 d007 64c0 7 48 d003 6500 c003 1050 e000 f000
  //   opCode
endmodule

module RegisterFile (
  input  enable,
  input  writeEnable,
  input  [2:0] readReg1,
  input  [2:0] readReg2,
  input  [2:0] writeReg,
  input  [15:0] writeData,
  input  clock,
  output [15:0] Data1,
  output [15:0] Data2
);

  wire and_1_out, decoder_1_out0, decoder_1_out1, decoder_1_out2, decoder_1_out3, decoder_1_out4,
       decoder_1_out5, decoder_1_out6, decoder_1_out7;
  wire [15:0] r1_q, r2_q, r3_q, r4_q, r5_q, r6_q, r7_q, r8_q;

  and and_1 (and_1_out, enable, writeEnable);
  Decoder #(.select(3)) decoder_1 (
    .out0(decoder_1_out0), .out1(decoder_1_out1), .out2(decoder_1_out2), .out3(decoder_1_out3),
    .out4(decoder_1_out4), .out5(decoder_1_out5), .out6(decoder_1_out6), .out7(decoder_1_out7),
    .sel(writeReg), .en(and_1_out));
  Register #(.width(16)) r1 (.D(writeData), .en(decoder_1_out0), .Q(r1_q), .clk(clock));  // open: clr
  Register #(.width(16)) r2 (.D(writeData), .en(decoder_1_out1), .Q(r2_q), .clk(clock));  // open: clr
  Register #(.width(16)) r3 (.D(writeData), .en(decoder_1_out2), .Q(r3_q), .clk(clock));  // open: clr
  Register #(.width(16)) r4 (.D(writeData), .en(decoder_1_out3), .Q(r4_q), .clk(clock));  // open: clr
  Register #(.width(16)) r5 (.D(writeData), .en(decoder_1_out4), .Q(r5_q), .clk(clock));  // open: clr
  Register #(.width(16)) r6 (.D(writeData), .en(decoder_1_out5), .Q(r6_q), .clk(clock));  // open: clr
  Register #(.width(16)) r7 (.D(writeData), .en(decoder_1_out6), .Q(r7_q), .clk(clock));  // open: clr
  Register #(.width(16)) r8 (.D(writeData), .en(decoder_1_out7), .Q(r8_q), .clk(clock));  // open: clr
  Multiplexer #(.select(3), .width(16)) multiplexer_1 (
    .in0(r1_q), .in1(r2_q), .in2(r3_q), .in3(r4_q), .in4(r5_q), .in5(r6_q), .in6(r7_q), .in7(r8_q),
    .out(Data2), .sel(readReg2));
  Multiplexer #(.select(3), .width(16)) multiplexer_2 (
    .in0(r1_q), .in1(r2_q), .in2(r3_q), .in3(r4_q), .in4(r5_q), .in5(r6_q), .in6(r7_q), .in7(r8_q),
    .out(Data1), .sel(readReg1));
endmodule

module ControlLogic (
  input  [3:0] bits15to12,
  output RegDst,
  output Jump,
  output Branch,
  output MemRead,
  output M2R,
  output [2:0] ALUOp,
  output MemWrite,
  output ALUSrc,
  output RegWrite,
  output Li,
  output Call,
  output Rtn,
  output halt
);

  wire decoder_1_out1, decoder_1_out2, decoder_1_out3, decoder_1_out6, decoder_1_out7, decoder_1_out8,
       decoder_1_out9, decoder_1_out10, decoder_1_out11, or_4_out;

  Decoder #(.select(4)) decoder_1 (
    .out0(Li), .out1(decoder_1_out1), .out2(decoder_1_out2), .out3(decoder_1_out3), .out4(M2R),
    .out5(MemWrite), .out6(decoder_1_out6), .out7(decoder_1_out7), .out8(decoder_1_out8),
    .out9(decoder_1_out9), .out10(decoder_1_out10), .out11(decoder_1_out11), .out12(Jump), .out13(Call),
    .out14(Rtn), .out15(halt), .sel(bits15to12));  // open: en
  or or_1 (ALUOp[2], decoder_1_out10, decoder_1_out11);
  or or_2 (ALUOp[0], decoder_1_out9, decoder_1_out11, decoder_1_out3);
  or or_3 (ALUOp[1], decoder_1_out2, decoder_1_out9, decoder_1_out8, decoder_1_out3);
  or or_4 (or_4_out, Li, decoder_1_out7);
  or or_5 (RegDst, decoder_1_out1, decoder_1_out2, decoder_1_out3);
  or or_6 (ALUSrc, MemWrite, decoder_1_out8, decoder_1_out9, or_4_out);
  or or_7 (RegWrite, RegDst, decoder_1_out8, or_4_out, decoder_1_out9, decoder_1_out6, M2R);

  assign Branch = ALUOp[2];
  assign MemRead = M2R;
endmodule

module ALU (
  input  [15:0] operand1,
  input  [2:0] operation,
  input  [15:0] operand2,
  output [15:0] ALUResult,
  output BleBne
);

  wire and_2_out, and_3_out, comparator_1_eq, comparator_1_lt, comparator_2_eq, not_1_out, not_3_out,
       or_2_out;
  wire [15:0] adder_1_out, and_1_out, bit_extender_1_out, not_2_out, or_1_out;

  Adder #(.width(16)) adder_1 (.a(operand1), .b(operand2), .out(adder_1_out));  // open: cin, cout
  assign and_1_out = operand1 & operand2;  // AND_Gate and_1, 16 bits wide
  assign or_1_out = operand1 | operand2;  // OR_Gate or_1, 16 bits wide
  Comparator #(.width(16)) comparator_1 (
    .a(operand2), .b(operand1), .eq(comparator_1_eq), .lt(comparator_1_lt));  // open: gt
  not not_1 (not_1_out, comparator_2_eq);
  Comparator #(.width(16)) comparator_2 (.a(operand1), .b(operand2), .eq(comparator_2_eq));  // open: gt, lt
  assign not_2_out = ~bit_extender_1_out;  // NOT_Gate not_2, 16 bits wide
  or or_2 (or_2_out, comparator_1_eq, comparator_1_lt);
  Multiplexer #(.select(3), .width(16)) multiplexer_1 (
    .in0(adder_1_out), .in1(not_2_out), .in2(and_1_out), .in3(or_1_out), .in4(not_2_out), .in5(not_2_out),
    .in6(not_2_out), .in7(not_2_out), .out(ALUResult), .sel(operation));
  and and_2 (and_2_out, not_3_out, operation[2], or_2_out);
  and and_3 (and_3_out, operation[0], operation[2], not_1_out);
  not not_3 (not_3_out, operation[0]);
  Multiplexer multiplexer_2 (.in0(and_2_out), .in1(and_3_out), .out(BleBne), .sel(operation[0]));
  assign bit_extender_1_out = {{15{operation[2]}}, operation[2]};  // Bit_Extender bit_extender_1
endmodule

module ALUControl (
  input  [2:0] ALUOp,
  input  [2:0] funct,
  input  ALUCrtlEnable,
  output [2:0] operation
);

  wire [2:0] multiplexer_1_out;

  Multiplexer #(.width(3)) multiplexer_1 (.in0(funct), .in1(3'b000), .out(multiplexer_1_out), .sel(ALUCrtlEnable));
  assign operation = ALUOp | multiplexer_1_out;  // OR_Gate or_1, 3 bits wide
endmodule
